# Fritzing sketch arduino-nunchuck-servo (saved by Fritzing 0.7.7b)

parts:
  Arduino1 = Arduino
  J1 = Basic Servo
  Composants1 = Triple Axis Accelerometer Breakout - ADXL345

nets:
  GND: Arduino1.GND, J1.gnd, Composants1.GND
  N1: Arduino1.D11, J1.pulse
  3V3: Arduino1.3V3, Composants1.VCC
  +5V: Arduino1.+5V, J1.vcc
  N2: Arduino1.A4, Composants1.SDA
  N3: Arduino1.A5, Composants1.SCL
